# Fritzing sketch McLighting-NodeMCU_Board (saved by Fritzing 0.9.2b)
breadboards: 1

parts:
  U1 = NodeMCU V1.0
  neopixel1 = Neopixel Ring 12

nets:
  N1: U1.D1, neopixel1.IN
  GND: U1.GND, neopixel1.GND
  VIN: U1.Vin, neopixel1.VCC

custom parts:
  NodeMCU V1.0: ESP9266 based NodeMCU
  Neopixel Ring 12: Neopixel Ring x12
