# Fritzing sketch McLighting-NodeMCU_Board_Levelshifter (saved by Fritzing 0.9.2b)
breadboards: 1

parts:
  Bauteil1 = Logic Level Converter
  U3 = NodeMCU V1.0
  NEOPIXEL1 = Neopixel Strip -- White (30/m)
  JACK1 = 2.1mm Barrel Jack with Terminal Block
  C1 = Electrolytic Capacitor [capacitance=1000μF package="1010 [SMD, electrolytic]"]

nets:
  GND: Bauteil1.GND, U3.GND
  N1: Bauteil1.LV, U3.3V3
  N2: Bauteil1.TX_LV, U3.D1
  N3: Bauteil1.TX_HV, NEOPIXEL1.Din
  N4: Bauteil1.HV, U3.Vin
  N5: NEOPIXEL1.GND, JACK1.NEG, C1.+
  N6: NEOPIXEL1.+5V, JACK1.POS, C1.-

custom parts:
  NodeMCU V1.0: ESP9266 based NodeMCU
  Neopixel Strip -- White (30/m): These NeoPixel strips have 30 digitally-addressable pixel LEDs per meter and are very affordable and are only 12.5 mm wide, 10 mm if you remove the strip from the casing.
